// Logisim project tmi.circ as structural Verilog: 3 circuits, main circuit main
module main (
);

  \cell  cell_1 ();  // open: DATA_IN, DATA_OUT, DATA_IN_2, DATA_OUT_2
  \cell  cell_2 ();  // open: DATA_IN, DATA_OUT, DATA_IN_2, DATA_OUT_2
  \cell  cell_3 ();  // open: DATA_IN, DATA_OUT, DATA_IN_2, DATA_OUT_2
endmodule

module mem (
  input  W0,
  input  W1,
  input  W2,
  input  W3,
  input  W4,
  input  W5,
  input  W6,
  input  W7,
  input  R_W,
  input  CLK,
  input  RST,
  output R0,
  output R1,
  output R2,
  output R3,
  output R4,
  output R5,
  output R6,
  output R7
);

  wire and_1_out, and_2_out, and_3_out, and_4_out, and_5_out, and_6_out, and_7_out, and_8_out;

  and and_1 (and_1_out, W0, R_W);
  and and_2 (and_2_out, W1, R_W);
  and and_3 (and_3_out, W2, R_W);
  and and_4 (and_4_out, W3, R_W);
  and and_5 (and_5_out, W4, R_W);
  and and_6 (and_6_out, W5, R_W);
  and and_7 (and_7_out, W6, R_W);
  and and_8 (and_8_out, W7, R_W);
  D_Flip_Flop d_ff_1 (.clk(CLK), .D(and_1_out), .Q(R0), .reset(RST));  // open: Qn, preset, en
  D_Flip_Flop d_ff_2 (.clk(CLK), .D(and_2_out), .Q(R1), .reset(RST));  // open: Qn, preset, en
  D_Flip_Flop d_ff_3 (.clk(CLK), .D(and_3_out), .Q(R2), .reset(RST));  // open: Qn, preset, en
  D_Flip_Flop d_ff_4 (.clk(CLK), .D(and_4_out), .Q(R3), .reset(RST));  // open: Qn, preset, en
  D_Flip_Flop d_ff_5 (.clk(CLK), .D(and_5_out), .Q(R4), .reset(RST));  // open: Qn, preset, en
  D_Flip_Flop d_ff_6 (.clk(CLK), .D(and_6_out), .Q(R5), .reset(RST));  // open: Qn, preset, en
  D_Flip_Flop d_ff_7 (.clk(CLK), .D(and_7_out), .Q(R6), .reset(RST));  // open: Qn, preset, en
  D_Flip_Flop d_ff_8 (.clk(CLK), .D(and_8_out), .Q(R7), .reset(RST));  // open: Qn, preset, en
endmodule

module \cell  (
  input  [7:0] DATA_IN,
  input  [7:0] DATA_IN_2,
  output [7:0] DATA_OUT,
  output [7:0] DATA_OUT_2
);

  wire undriven_2, undriven_3, undriven_4;
  wire [7:0] mem_1_r0, undriven;

  LED HEAD ();  // open: in
  mem mem_1 (
    .W0(undriven[0]), .W1(undriven[1]), .W2(undriven[2]), .W3(undriven[3]), .W4(undriven[4]),
    .W5(undriven[5]), .W6(undriven[6]), .W7(undriven[7]), .R_W(undriven_2), .CLK(undriven_3),
    .RST(undriven_4), .R0(mem_1_r0[0]), .R1(mem_1_r0[1]), .R2(mem_1_r0[2]), .R3(mem_1_r0[3]),
    .R4(mem_1_r0[4]), .R5(mem_1_r0[5]), .R6(mem_1_r0[6]), .R7(mem_1_r0[7]));
  LED ACTIVE ();  // open: in
  Adder adder_1 ();  // open: a, b, out, cin, cout
  LED TAIL ();  // open: in

  assign DATA_IN_2 = DATA_IN;
  assign DATA_OUT_2 = DATA_OUT;
endmodule
